# Fritzing sketch booster (saved by Fritzing 0.9.2b)
breadboards: 1

parts:
  IC1 = IC, DIP package, 20 pins [chip_label=L6202]
  C1 = Ceramic Capacitor [capacitance=10nF package="100 mil [THT, multilayer]"]
  C2 = Ceramic Capacitor [capacitance=10nF package="100 mil [THT, multilayer]"]

nets:
  N1: IC1.pin1, IC1.pin4, IC1.pin5, IC1.pin6, IC1.pin7, IC1.pin14, IC1.pin15, IC1.pin16, IC1.pin17
  N2: IC1.pin9, C2.1
  N3: IC1.pin11, C1.0
  N4: IC1.pin12, C1.1
  N5: IC1.pin19, C2.0
